// Logisim project WargnierPierre.circ as structural Verilog: 11 circuits, main circuit add
module main (
  input  in_1,
  input  in_2
);

  wire and_1_out, comparator_1_eq, emem, ereg, not_1_out, not_2_out, rscp, rtlmm, rtrd, ualmem;
  wire [3:0] Op;
  wire [4:0] multiplexer_1_out, shamt;
  wire [5:0] C0, Nf;
  wire [25:11] MEMI_out_2;
  wire [31:0] adder_1_out, bit_extender_1_out, cp_out_4, MEM_D_out_6, multiplexer_2_out, multiplexer_3_out,
       multiplexer_4_out, multiplexer_5_out, multiplexer_6_out, Registre_out_8, Registre_out_9,
       Registre_out_10, Registre_out_11, Registre_out_12, Registre_out_13, shifter_1_out, UAL_out_5;

  // Probe on C0
  // Probe on Nf
  // Probe on multiplexer_6_out
  cp cp (.in_1(multiplexer_6_out), .clock(not_1_out), ._0(in_2), .out_4(cp_out_4));
  not not_1 (not_1_out, in_1);
  CMD CMD (.in_1(Nf), .in_2(C0), .out_3(Op), .out_4({ualmem, emem, ereg, rtlmm, rscp, rtrd}));
  Adder #(.width(32)) adder_1 (.a(32'h4), .b(cp_out_4), .out(adder_1_out));  // open: cin, cout
  MEMI MEMI (.in_1(cp_out_4), .out_2({C0, MEMI_out_2, shamt, Nf}));
  // Probe on cp_out_4
  // Probe on Op
  // Probe on {ualmem, emem, ereg, rtlmm, rscp, rtrd}
  // Probe on {C0, MEMI_out_2, shamt, Nf}
  // Probe on Registre_out_12
  // Probe on Registre_out_11
  // Probe on Registre_out_10
  // Probe on Registre_out_13
  // Probe on MEMI_out_2[20:16]
  // Probe on MEMI_out_2[25:21]
  assign bit_extender_1_out = {{16{1'b0}}, {MEMI_out_2[15:11], shamt, Nf}};  // Bit_Extender bit_extender_1
  // Probe on multiplexer_1_out
  Multiplexer #(.width(5), .enable("false")) multiplexer_1 (
    .in0(MEMI_out_2[20:16]), .in1(MEMI_out_2[15:11]), .out(multiplexer_1_out), .sel(rtrd));
  Shifter #(.width(32)) shifter_1 (.in(bit_extender_1_out), .\dist (5'b00010), .out(shifter_1_out));
  Multiplexer #(.width(32), .enable("false")) multiplexer_2 (
    .in0(bit_extender_1_out), .in1(shifter_1_out), .out(multiplexer_2_out), .sel(rscp));
  Comparator #(.width(32)) comparator_1 (.a(Registre_out_8), .b(Registre_out_9), .eq(comparator_1_eq));  // open: gt, lt
  registre Registre (
    .in_1(in_1), .in_2(in_2), .in_3(multiplexer_3_out), .in_6(1'b1), .in_7(multiplexer_1_out),
    .out_8(Registre_out_8), .in_4(MEMI_out_2[25:21]), .out_9(Registre_out_9), .in_5(MEMI_out_2[20:16]),
    .out_10(Registre_out_10), .out_11(Registre_out_11), .out_12(Registre_out_12), .out_13(Registre_out_13));
  Multiplexer #(.width(32), .enable("false")) multiplexer_3 (
    .in0(UAL_out_5), .in1(MEM_D_out_6), .out(multiplexer_3_out), .sel(ualmem));
  not not_2 (not_2_out, comparator_1_eq);
  // Probe on multiplexer_4_out
  Multiplexer #(.width(32), .enable("false")) multiplexer_4 (
    .in0(Registre_out_8), .in1(adder_1_out), .out(multiplexer_4_out), .sel(rscp));
  Multiplexer #(.width(32), .enable("false")) multiplexer_5 (
    .in0(Registre_out_9), .in1(multiplexer_2_out), .out(multiplexer_5_out), .sel(rtlmm));
  // Probe on multiplexer_5_out
  and and_1 (and_1_out, not_2_out, rscp);
  Multiplexer #(.width(32), .enable("false")) multiplexer_6 (
    .in0(adder_1_out), .in1(UAL_out_5), .out(multiplexer_6_out), .sel(and_1_out));
  UAL UAL (.in_1(multiplexer_4_out), .in_2(multiplexer_5_out), .in_3(shamt), .out_5(UAL_out_5), .in_4(Op));
  MEMD MEM_D (.in_1(UAL_out_5), .in_2(Registre_out_9), .in_3(emem), .in_4(in_1), .in_5(in_2), .out_6(MEM_D_out_6));
  // Probe on UAL_out_5

  // Other names for the same wires on the sheet: H = in_1; rst = in_2
endmodule

// +
module add (
  input  in_1,
  input  [3:0] in_2,
  input  [3:0] in_3,
  output [3:0] out_4,
  output out_5
);

  wire add_complet_nand_2_r, add_complet_nand_3_r, add_complet_nand_4_r;

  add_complet_nand add_complet_nand_1 (.a(in_2[3]), .b(in_3[3]), .ci(add_complet_nand_2_r), .co(out_4[3]), .r(out_5));
  add_complet_nand add_complet_nand_2 (
    .a(in_2[2]), .b(in_3[2]), .ci(add_complet_nand_3_r), .co(out_4[2]), .r(add_complet_nand_2_r));
  add_complet_nand add_complet_nand_3 (
    .a(in_2[1]), .b(in_3[1]), .ci(add_complet_nand_4_r), .co(out_4[1]), .r(add_complet_nand_3_r));
  add_complet_nand add_complet_nand_4 (.a(in_2[0]), .b(in_3[0]), .ci(in_1), .co(out_4[0]), .r(add_complet_nand_4_r));
endmodule

module add32bits (
  input  [31:0] \donnée_1 ,
  input  retenue_entrante,
  input  [31:0] \donnée_2 ,
  output reteune_sortante,
  output [31:0] sortie
);

  wire add_2_out_5, add_3_out_5, add_4_out_5, add_5_out_5, add_6_out_5, add_7_out_5, add_8_out_5;

  add add_1 (
    .in_1(add_2_out_5), .in_2(\donnée_1 [31:28]), .in_3(\donnée_2 [31:28]), .out_4(sortie[31:28]),
    .out_5(reteune_sortante));
  add add_2 (
    .in_1(add_3_out_5), .in_2(\donnée_1 [27:24]), .in_3(\donnée_2 [27:24]), .out_4(sortie[27:24]),
    .out_5(add_2_out_5));
  add add_3 (
    .in_1(add_4_out_5), .in_2(\donnée_1 [23:20]), .in_3(\donnée_2 [23:20]), .out_4(sortie[23:20]),
    .out_5(add_3_out_5));
  add add_4 (
    .in_1(add_5_out_5), .in_2(\donnée_1 [19:16]), .in_3(\donnée_2 [19:16]), .out_4(sortie[19:16]),
    .out_5(add_4_out_5));
  add add_5 (
    .in_1(add_6_out_5), .in_2(\donnée_1 [15:12]), .in_3(\donnée_2 [15:12]), .out_4(sortie[15:12]),
    .out_5(add_5_out_5));
  add add_6 (
    .in_1(add_7_out_5), .in_2(\donnée_1 [11:8]), .in_3(\donnée_2 [11:8]), .out_4(sortie[11:8]),
    .out_5(add_6_out_5));
  add add_7 (
    .in_1(add_8_out_5), .in_2(\donnée_1 [7:4]), .in_3(\donnée_2 [7:4]), .out_4(sortie[7:4]),
    .out_5(add_7_out_5));
  add add_8 (
    .in_1(retenue_entrante), .in_2(\donnée_1 [3:0]), .in_3(\donnée_2 [3:0]), .out_4(sortie[3:0]),
    .out_5(add_8_out_5));

  // Notes on the sheet:
  //   retenue_entrante: pull=down
endmodule

module lui (
  input  [31:0] in_1,
  output [31:0] out_2
);

  Shifter #(.width(32)) shifter_1 (.in(in_1), .\dist (5'b10000), .out(out_2));
endmodule

module UAL (
  input  [31:0] in_1,
  input  [31:0] in_2,
  input  [4:0] in_3,
  input  [3:0] in_4,
  output [31:0] out_5
);

  wire [31:0] add32bits_sortie, and_out, lui_out_2, nor_out, or_out, shifter_1_out, shifter_2_out,
       shifter_3_out, subtractor_1_out, xor_out;

  Shifter #(.width(32)) shifter_1 (.in(in_2), .\dist (in_3), .out(shifter_1_out));
  assign and_out = in_1 & in_2;  // AND_Gate and, 32 bits wide
  Shifter #(.width(32), .shift("ar")) shifter_2 (.in(in_2), .\dist (in_3), .out(shifter_2_out));
  assign nor_out = ~(in_1 | in_2);  // NOR_Gate nor, 32 bits wide
  Subtractor #(.width(32)) subtractor_1 (.a(in_1), .b(in_2), .out(subtractor_1_out));  // open: bin, bout
  add32bits add32bits (
    .\donnée_1 (in_1), .\donnée_2 (in_2), .sortie(add32bits_sortie));  // open: retenue_entrante, reteune_sortante
  Shifter #(.width(32), .shift("lr")) shifter_3 (.in(in_1), .\dist (in_3), .out(shifter_3_out));
  assign or_out = in_1 | in_2;  // OR_Gate or, 32 bits wide
  lui lui (.in_1(in_1), .out_2(lui_out_2));
  assign xor_out = in_1 ^ in_2;  // XOR_Gate xor, 32 bits wide
  Multiplexer #(.select(4), .width(32), .enable("false")) multiplexer_1 (
    .in0(xor_out), .in1(shifter_1_out), .in2(and_out), .in3(shifter_2_out), .in4(nor_out),
    .in5(subtractor_1_out), .in6(add32bits_sortie), .in7(shifter_3_out), .in8(or_out), .in9(lui_out_2),
    .out(out_5), .sel(in_4));  // open: in10, in11, in12, in13, in14, in15
endmodule

module MEMI (
  input  [31:0] in_1,
  output [31:0] out_2
);

  ROM #(.addrWidth(14), .dataWidth(32)) rom_1 (.addr(in_1[15:2]), .data(out_2), .sel(1'b1));

  // Notes on the sheet:
  //   contents of rom_1 (hex, n*v repeats v):
  //   3c010000 3421ffff 14820 ad090000 8d020000 24100 20010001 1014822 1408fffd
endmodule

module MEMD (
  input  [31:0] in_1,
  input  [31:0] in_2,
  input  in_3,
  input  in_4,
  input  in_5,
  output [31:0] out_6
);

  RAM #(.addrWidth(14), .dataWidth(32), .bus("separate")) ram_1 (
    .addr(in_1[15:2]), .din(in_2), .data(out_6), .str(in_3), .sel(1'b1), .clk(in_4), .ld(1'b1), .clr(in_5));
endmodule

module add_complet_nand (
  input  a,
  input  b,
  input  ci,
  output co,
  output r
);

  wire nand_1_out, nand_2_out, nand_3_out, nand_4_out, nand_5_out, nand_6_out, nand_7_out, nand_8_out,
       nand_9_out, nand_10_out;

  nand nand_1 (nand_1_out, a, a);
  nand nand_2 (nand_2_out, b, b);
  nand nand_3 (nand_3_out, ci, ci);
  nand nand_4 (nand_4_out, a, b);
  nand nand_5 (nand_5_out, a, ci);
  nand nand_6 (nand_6_out, b, ci);
  nand nand_7 (nand_7_out, nand_3_out, nand_1_out, b);
  nand nand_8 (nand_8_out, nand_3_out, a, nand_2_out);
  nand nand_9 (nand_9_out, ci, nand_2_out, nand_1_out);
  nand nand_10 (nand_10_out, ci, b, a);
  nand nand_11 (co, nand_4_out, nand_5_out, nand_6_out);
  nand nand_12 (r, nand_7_out, nand_8_out, nand_9_out, nand_10_out);
endmodule

module CMD (
  input  [5:0] in_1,
  input  [5:0] in_2,
  output [3:0] out_3,
  output [5:0] out_4
);

  wire add, addi, \and , and_1_out, and_2_out, andi, lui, \nor , not_1_out, \or , or_1_out, or_2_out,
       or_3_out, or_4_out, ori, sll, sra, srl, sub, \xor , xori;

  or or_1 (or_1_out, \and , andi);
  Decoder #(.select(5), .disabled(0)) decoder_1 (
    .out3(out_4[5]), .out11(out_4[4]), .sel(in_2[4:0]), .en(in_2[5]));  // open: out0, out1, out2, out4, out5, out6, out7, out8, out9, out10, out12, out13, out14, out15, out16, out17, out18, out19, out20, out21, out22, out23, out24, out25, out26, out27, out28, out29, out30, out31
  Decoder #(.select(5), .disabled(0)) decoder_2 (
    .out0(out_4[0]), .out5(out_4[1]), .out8(addi), .out12(andi), .out13(ori), .out14(xori), .out15(lui),
    .sel(in_2[4:0]), .en(not_1_out));  // open: out1, out2, out3, out4, out6, out7, out9, out10, out11, out16, out17, out18, out19, out20, out21, out22, out23, out24, out25, out26, out27, out28, out29, out30, out31
  or or_2 (or_2_out, \xor , xori);
  or or_3 (or_3_out, add, addi, out_4[5], out_4[4], out_4[1]);
  or or_4 (or_4_out, \or , ori);
  Decoder #(.select(5), .disabled(0)) decoder_3 (
    .out0(add), .out2(sub), .out4(\and ), .out5(\or ), .out6(\xor ), .out7(\nor ), .sel(in_1[4:0]),
    .en(and_1_out));  // open: out1, out3, out8, out9, out10, out11, out12, out13, out14, out15, out16, out17, out18, out19, out20, out21, out22, out23, out24, out25, out26, out27, out28, out29, out30, out31
  and and_1 (and_1_out, in_1[5], out_4[0]);
  Decoder #(.select(5), .disabled(0)) decoder_4 (
    .out0(sll), .out2(srl), .out3(sra), .sel(in_1[4:0]), .en(and_2_out));  // open: out1, out4, out5, out6, out7, out8, out9, out10, out11, out12, out13, out14, out15, out16, out17, out18, out19, out20, out21, out22, out23, out24, out25, out26, out27, out28, out29, out30, out31
  not not_1 (not_1_out, in_2[5]);
  and and_2 (and_2_out, ~in_1[5], out_4[0]);  // AND_Gate
  Priority_Encoder #(.select(4), .disabled(0)) priority_encoder_1 (
    .in0(or_2_out), .in1(sll), .in2(or_1_out), .in3(sra), .in4(\nor ), .in5(sub), .in6(or_3_out), .in7(srl),
    .in8(or_4_out), .in9(lui), .out(out_3));  // open: in10, in11, in12, in13, in14, in15, gs, en_out, en_in
  nor nor_1 (out_4[3], out_4[1], out_4[4]);
  not not_2 (out_4[2], out_4[0]);

  // Other names for the same wires on the sheet: R = out_4[0]; bne = out_4[1]; sw = out_4[4]; lw = out_4[5]
endmodule

module cp (
  input  [31:0] in_1,
  input  clock,
  input  _0,
  output [31:0] out_4
);

  Register #(.width(16)) register_1 (.D(in_1[15:0]), .en(1'b1), .Q(out_4[15:0]), .clk(clock), .clr(_0));

  assign out_4[31:16] = 16'h40;
endmodule

module registre (
  input  in_1,
  input  in_2,
  input  [31:0] in_3,
  input  [4:0] in_4,
  input  [4:0] in_5,
  input  in_6,
  input  [4:0] in_7,
  output [31:0] out_8,
  output [31:0] out_9,
  output [31:0] out_10,
  output [31:0] out_11,
  output [31:0] out_12,
  output [31:0] out_13
);

  wire decoder_1_out1, decoder_1_out2, decoder_1_out4, decoder_1_out8, decoder_1_out9, decoder_1_out10,
       decoder_1_out11, decoder_1_out12, decoder_1_out13, decoder_1_out14, decoder_1_out15, decoder_1_out31;
  wire [31:0] _3, _6, _7, _8, _9, _10, _11, _12;

  Decoder #(.select(5)) decoder_1 (
    .out1(decoder_1_out1), .out2(decoder_1_out2), .out4(decoder_1_out4), .out8(decoder_1_out8),
    .out9(decoder_1_out9), .out10(decoder_1_out10), .out11(decoder_1_out11), .out12(decoder_1_out12),
    .out13(decoder_1_out13), .out14(decoder_1_out14), .out15(decoder_1_out15), .out31(decoder_1_out31),
    .sel(in_7), .en(in_6));  // open: out0, out3, out5, out6, out7, out16, out17, out18, out19, out20, out21, out22, out23, out24, out25, out26, out27, out28, out29, out30
  Register #(.width(32)) v0 (.D(in_3), .en(decoder_1_out2), .Q(out_10), .clk(in_1), .clr(in_2));
  Register #(.width(32)) a0 (.D(in_3), .en(decoder_1_out4), .Q(out_11), .clk(in_1), .clr(in_2));
  Register #(.width(32)) at (.D(in_3), .en(decoder_1_out1), .Q(_3), .clk(in_1), .clr(in_2));
  Register #(.width(32)) t0 (.D(in_3), .en(decoder_1_out8), .Q(out_12), .clk(in_1), .clr(in_2));
  Register #(.width(32)) t1 (.D(in_3), .en(decoder_1_out9), .Q(out_13), .clk(in_1), .clr(in_2));
  Register #(.width(32)) t2 (.D(in_3), .en(decoder_1_out10), .Q(_6), .clk(in_1), .clr(in_2));
  Register #(.width(32)) t3 (.D(in_3), .en(decoder_1_out11), .Q(_7), .clk(in_1), .clr(in_2));
  Register #(.width(32)) t4 (.D(in_3), .en(decoder_1_out12), .Q(_8), .clk(in_1), .clr(in_2));
  Register #(.width(32)) t5 (.D(in_3), .en(decoder_1_out13), .Q(_9), .clk(in_1), .clr(in_2));
  Register #(.width(32)) t6 (.D(in_3), .en(decoder_1_out14), .Q(_10), .clk(in_1), .clr(in_2));
  Register #(.width(32)) t7 (.D(in_3), .en(decoder_1_out15), .Q(_11), .clk(in_1), .clr(in_2));
  Register #(.width(32)) ra (.D(in_3), .en(decoder_1_out31), .Q(_12), .clk(in_1), .clr(in_2));
  Multiplexer #(.select(5), .width(32), .enable("false")) multiplexer_1 (
    .in0({32{1'b0}}), .in1(_3), .in2(out_10), .in4(out_11), .in8(out_12), .in9(out_13), .in10(_6), .in11(_7),
    .in12(_8), .in13(_9), .in14(_10), .in15(_11), .in31(_12), .out(out_8), .sel(in_4));  // open: in3, in5, in6, in7, in16, in17, in18, in19, in20, in21, in22, in23, in24, in25, in26, in27, in28, in29, in30
  Multiplexer #(.select(5), .width(32), .enable("false")) multiplexer_2 (
    .in0({32{1'b0}}), .in1(_3), .in2(out_10), .in4(out_11), .in8(out_12), .in9(out_13), .in10(_6), .in11(_7),
    .in12(_8), .in13(_9), .in14(_10), .in15(_11), .in31(_12), .out(out_9), .sel(in_5));  // open: in3, in5, in6, in7, in16, in17, in18, in19, in20, in21, in22, in23, in24, in25, in26, in27, in28, in29, in30

  // Other names for the same wires on the sheet: _1[31:0] = out_10; _2[31:0] = out_11; _4[31:0] = out_12;
  //   _5[31:0] = out_13
endmodule
