// Logisim project logi1.circ as structural Verilog
module main (
  input  in_1,
  input  in_2,
  input  in_3,
  input  in_4,
  output out_5,
  output out_6,
  output out_7,
  output out_8,
  output out_9,
  output [31:0] out_10
);

  wire co, demi_add_1_r, demi_add_2_c;

  Multiplexer multiplexer_1 (.out(out_9), .en(in_4));  // open: in0, in1, sel
  // Probe on demi_add_1_r
  demi_add demi_add_1 (.a(in_1), .r(demi_add_1_r), .c(co), .b(in_2));
  demi_add demi_add_2 (.a(demi_add_1_r), .r(out_7), .c(demi_add_2_c), .b(in_3));
  or or_1 (out_8, co, demi_add_2_c);

  assign out_5 = 1'b1;
  assign out_6 = 1'b0;
  assign out_10 = {32{1'b1}};
endmodule

// +
module demi_add (
  input  a,
  input  b,
  output r,
  output c
);

  and and_1 (c, a, b);
  xor xor_1 (r, a, b);
endmodule
