// Logisim project non_signe_enonce.circ as structural Verilog: 10 circuits, main circuit rotation-gauche-1-rang
module rotation_gauche_1_rang (
  input  [31:0] \donnée ,
  output [31:0] \résultat 
);

  wire [31:0] shifter_1_out, shifter_2_out;

  Shifter #(.width(32)) shifter_1 (.in(\donnée ), .\dist (5'b00001), .out(shifter_1_out));
  Shifter #(.width(32), .shift("lr")) shifter_2 (.in(\donnée ), .\dist ({5{1'b1}}), .out(shifter_2_out));
  assign \résultat  = shifter_1_out | shifter_2_out;  // OR_Gate or_1, 32 bits wide
endmodule

module rotation_droite_1_rang (
  input  [31:0] \donnée ,
  output [31:0] \résultat 
);

  wire [31:0] shifter_1_out, shifter_2_out;

  Shifter #(.width(32)) shifter_1 (.in(\donnée ), .\dist (5'b00001), .out(shifter_1_out));
  Shifter #(.width(32), .shift("lr")) shifter_2 (.in(\donnée ), .\dist (5'b00001), .out(shifter_2_out));
  assign \résultat  = shifter_1_out | shifter_2_out;  // OR_Gate or_1, 32 bits wide
endmodule

module rotation_gauche_n_rangs (
  input  [31:0] \donnée ,
  input  [4:0] n,
  output [31:0] \résultat 
);

  wire [4:0] subtractor_1_out;
  wire [31:0] shifter_1_out, shifter_2_out;

  Subtractor #(.width(5)) subtractor_1 (.a({5{1'b0}}), .b(n), .out(subtractor_1_out));  // open: bin, bout
  Shifter #(.width(32)) shifter_1 (.in(\donnée ), .\dist (n), .out(shifter_1_out));
  Shifter #(.width(32), .shift("lr")) shifter_2 (.in(\donnée ), .\dist (subtractor_1_out), .out(shifter_2_out));
  assign \résultat  = shifter_1_out | shifter_2_out;  // OR_Gate or_1, 32 bits wide
endmodule

module rotation_droite_n_rangs (
  input  [31:0] \donnée ,
  input  [4:0] n,
  output [31:0] \résultat 
);

  wire [4:0] subtractor_1_out;
  wire [31:0] shifter_1_out, shifter_2_out;

  Subtractor #(.width(5)) subtractor_1 (.a({5{1'b0}}), .b(n), .out(subtractor_1_out));  // open: bin, bout
  Shifter #(.width(32), .shift("rr")) shifter_1 (.in(\donnée ), .\dist (n), .out(shifter_1_out));
  Shifter #(.width(32), .shift("rr")) shifter_2 (.in(\donnée ), .\dist (subtractor_1_out), .out(shifter_2_out));
  assign \résultat  = shifter_1_out | shifter_2_out;  // OR_Gate or_1, 32 bits wide
endmodule

module egal_v1 (
  input  [31:0] a,
  input  [31:0] b,
  output egal
);

  wire [31:0] xnor_1_out;

  assign xnor_1_out = ~(a ^ b);  // XNOR_Gate xnor_1, 32 bits wide
  and and_1 (egal, xnor_1_out[0], xnor_1_out[1], xnor_1_out[2], xnor_1_out[3], xnor_1_out[4], xnor_1_out[5], xnor_1_out[6], xnor_1_out[7], xnor_1_out[8], xnor_1_out[9], xnor_1_out[10], xnor_1_out[11], xnor_1_out[12], xnor_1_out[13], xnor_1_out[14], xnor_1_out[15], xnor_1_out[16], xnor_1_out[17], xnor_1_out[18], xnor_1_out[19], xnor_1_out[20], xnor_1_out[21], xnor_1_out[22], xnor_1_out[23], xnor_1_out[24], xnor_1_out[25], xnor_1_out[26], xnor_1_out[27], xnor_1_out[28], xnor_1_out[29], xnor_1_out[30], xnor_1_out[31]);
endmodule

module egal_v2 (
  input  [31:0] a,
  input  [31:0] b,
  output egal
);

  wire nand_6_out;
  wire [31:0] nand_1_out, nand_2_out, nand_3_out, nand_4_out, nand_5_out;

  assign nand_1_out = ~({32{1'b1}} & a);  // NAND_Gate nand_1, 32 bits wide
  assign nand_2_out = ~(b & {32{1'b1}});  // NAND_Gate nand_2, 32 bits wide
  assign nand_3_out = ~(a & b);  // NAND_Gate nand_3, 32 bits wide
  assign nand_4_out = ~(nand_1_out & nand_2_out);  // NAND_Gate nand_4, 32 bits wide
  assign nand_5_out = ~(nand_3_out & nand_4_out);  // NAND_Gate nand_5, 32 bits wide
  nand nand_6 (nand_6_out, nand_5_out[0], nand_5_out[1], nand_5_out[2], nand_5_out[3], nand_5_out[4], nand_5_out[5], nand_5_out[6], nand_5_out[7], nand_5_out[8], nand_5_out[9], nand_5_out[10], nand_5_out[11], nand_5_out[12], nand_5_out[13], nand_5_out[14], nand_5_out[15], nand_5_out[16], nand_5_out[17], nand_5_out[18], nand_5_out[19], nand_5_out[20], nand_5_out[21], nand_5_out[22], nand_5_out[23], nand_5_out[24], nand_5_out[25], nand_5_out[26], nand_5_out[27], nand_5_out[28], nand_5_out[29], nand_5_out[30], nand_5_out[31]);
  nand nand_7 (egal, nand_6_out, nand_6_out);
endmodule

// +
module add_complet_nand (
  input  a,
  input  b,
  input  ci,
  output co,
  output r
);

  wire nand_1_out, nand_2_out, nand_3_out, nand_4_out, nand_5_out, nand_6_out, nand_7_out, nand_8_out,
       nand_9_out, nand_10_out;

  nand nand_1 (nand_1_out, a, a);
  nand nand_2 (nand_2_out, b, b);
  nand nand_3 (nand_3_out, ci, ci);
  nand nand_4 (nand_4_out, a, b);
  nand nand_5 (nand_5_out, a, b);
  nand nand_6 (nand_6_out, a, b);
  nand nand_7 (nand_7_out, nand_3_out, nand_1_out, b);
  nand nand_8 (nand_8_out, nand_3_out, a, nand_2_out);
  nand nand_9 (nand_9_out, ci, nand_2_out, nand_1_out);
  nand nand_10 (nand_10_out, ci, b, a);
  nand nand_11 (co, nand_4_out, nand_5_out, nand_6_out);
  nand nand_12 (r, nand_7_out, nand_8_out, nand_9_out, nand_10_out);
endmodule

// +
module add_4_bits (
  input  retenue_entrante,
  input  [3:0] \donnée_1 ,
  input  [3:0] \donnée_2 ,
  output [3:0] \résultat ,
  output retenue_sortante
);

  wire adder_2_cout, adder_3_cout, adder_4_cout;

  Adder #(.width(1)) adder_1 (
    .a(\donnée_1 [3]), .b(\donnée_2 [3]), .out(\résultat [3]), .cin(adder_2_cout), .cout(retenue_sortante));
  Adder #(.width(1)) adder_2 (
    .a(\donnée_1 [2]), .b(\donnée_2 [2]), .out(\résultat [2]), .cin(adder_3_cout), .cout(adder_2_cout));
  Adder #(.width(1)) adder_3 (
    .a(\donnée_1 [1]), .b(\donnée_2 [1]), .out(\résultat [1]), .cin(adder_4_cout), .cout(adder_3_cout));
  Adder #(.width(1)) adder_4 (
    .a(\donnée_1 [0]), .b(\donnée_2 [0]), .out(\résultat [0]), .cin(retenue_entrante), .cout(adder_4_cout));
endmodule

module add_32_bits (
  input  [31:0] \donnée_1 ,
  input  retenue_entrante,
  input  [31:0] \donnée_2 ,
  output reteune_sortante,
  output [31:0] sortie
);

  wire add_4_bits_2_retenue_sortante, add_4_bits_3_retenue_sortante, add_4_bits_4_retenue_sortante,
       add_4_bits_5_retenue_sortante, add_4_bits_6_retenue_sortante, add_4_bits_7_retenue_sortante,
       add_4_bits_8_retenue_sortante;

  add_4_bits add_4_bits_1 (
    .retenue_entrante(add_4_bits_2_retenue_sortante), .\donnée_1 (\donnée_1 [31:28]),
    .\donnée_2 (\donnée_2 [31:28]), .\résultat (sortie[31:28]), .retenue_sortante(reteune_sortante));
  add_4_bits add_4_bits_2 (
    .retenue_entrante(add_4_bits_3_retenue_sortante), .\donnée_1 (\donnée_1 [27:24]),
    .\donnée_2 (\donnée_2 [27:24]), .\résultat (sortie[27:24]),
    .retenue_sortante(add_4_bits_2_retenue_sortante));
  add_4_bits add_4_bits_3 (
    .retenue_entrante(add_4_bits_4_retenue_sortante), .\donnée_1 (\donnée_1 [23:20]),
    .\donnée_2 (\donnée_2 [23:20]), .\résultat (sortie[23:20]),
    .retenue_sortante(add_4_bits_3_retenue_sortante));
  add_4_bits add_4_bits_4 (
    .retenue_entrante(add_4_bits_5_retenue_sortante), .\donnée_1 (\donnée_1 [19:16]),
    .\donnée_2 (\donnée_2 [19:16]), .\résultat (sortie[19:16]),
    .retenue_sortante(add_4_bits_4_retenue_sortante));
  add_4_bits add_4_bits_5 (
    .retenue_entrante(add_4_bits_6_retenue_sortante), .\donnée_1 (\donnée_1 [15:12]),
    .\donnée_2 (\donnée_2 [15:12]), .\résultat (sortie[15:12]),
    .retenue_sortante(add_4_bits_5_retenue_sortante));
  add_4_bits add_4_bits_6 (
    .retenue_entrante(add_4_bits_7_retenue_sortante), .\donnée_1 (\donnée_1 [11:8]),
    .\donnée_2 (\donnée_2 [11:8]), .\résultat (sortie[11:8]), .retenue_sortante(add_4_bits_6_retenue_sortante));
  add_4_bits add_4_bits_7 (
    .retenue_entrante(add_4_bits_8_retenue_sortante), .\donnée_1 (\donnée_1 [7:4]),
    .\donnée_2 (\donnée_2 [7:4]), .\résultat (sortie[7:4]), .retenue_sortante(add_4_bits_7_retenue_sortante));
  add_4_bits add_4_bits_8 (
    .retenue_entrante(retenue_entrante), .\donnée_1 (\donnée_1 [3:0]), .\donnée_2 (\donnée_2 [3:0]),
    .\résultat (sortie[3:0]), .retenue_sortante(add_4_bits_8_retenue_sortante));
endmodule

module fast_comp_32 (
  input  [31:0] \donnée ,
  output [31:0] \résultat 
);

  wire [31:0] adder_1_out, adder_2_out, adder_4_out, adder_5_out, and_1_out, and_2_out, and_3_out, and_4_out,
       and_5_out, and_6_out, and_7_out, and_8_out, and_9_out, and_10_out, shifter_1_out, shifter_2_out,
       shifter_3_out, shifter_4_out, shifter_5_out;

  Shifter #(.width(32)) shifter_1 (.in(\donnée ), .\dist (5'b00001), .out(shifter_1_out));
  Shifter #(.width(32)) shifter_2 (.in(adder_4_out), .\dist (5'b00100), .out(shifter_2_out));
  Shifter #(.width(32)) shifter_3 (.in(adder_5_out), .\dist (5'b10000), .out(shifter_3_out));
  assign and_1_out = \donnée  & 32'h55555555;  // AND_Gate and_1, 32 bits wide
  Adder #(.width(32)) adder_1 (.a(and_1_out), .b(and_2_out), .out(adder_1_out));  // open: cin, cout
  assign and_2_out = shifter_1_out & 32'h55555555;  // AND_Gate and_2, 32 bits wide
  assign and_3_out = adder_4_out & 32'hf0f0f0f;  // AND_Gate and_3, 32 bits wide
  Adder #(.width(32)) adder_2 (.a(and_3_out), .b(and_4_out), .out(adder_2_out));  // open: cin, cout
  assign and_4_out = shifter_2_out & 32'hf0f0f0f;  // AND_Gate and_4, 32 bits wide
  assign and_5_out = adder_5_out & 32'hffff;  // AND_Gate and_5, 32 bits wide
  Adder #(.width(32)) adder_3 (.a(and_5_out), .b(and_6_out), .out(\résultat ));  // open: cin, cout
  assign and_6_out = shifter_3_out & 32'hffff;  // AND_Gate and_6, 32 bits wide
  Shifter #(.width(32), .shift("lr")) shifter_4 (.in(adder_1_out), .\dist (5'b00010), .out(shifter_4_out));
  Shifter #(.width(32), .shift("lr")) shifter_5 (.in(adder_2_out), .\dist (5'b01000), .out(shifter_5_out));
  assign and_7_out = adder_1_out & 32'h33333333;  // AND_Gate and_7, 32 bits wide
  assign and_8_out = shifter_4_out & 32'h33333333;  // AND_Gate and_8, 32 bits wide
  assign and_9_out = adder_2_out & 32'hff00ff;  // AND_Gate and_9, 32 bits wide
  assign and_10_out = shifter_5_out & 32'hff00ff;  // AND_Gate and_10, 32 bits wide
  Adder #(.width(32)) adder_4 (.a(and_7_out), .b(and_8_out), .out(adder_4_out));  // open: cin, cout
  Adder #(.width(32)) adder_5 (.a(and_9_out), .b(and_10_out), .out(adder_5_out));  // open: cin, cout
endmodule
