// Logisim project test.circ as structural Verilog
module UAL (
  input  [31:0] in_1,
  input  [31:0] in_2,
  input  [31:0] in_3,
  input  [4:0] in_4,
  input  [3:0] in_5
);

  wire [31:0] adder_1_out, and_1_out, shifter_1_out, xor_1_out;

  Adder #(.width(32)) adder_1 (.a(in_1), .b(in_3), .out(adder_1_out));  // open: cin, cout
  assign and_1_out = in_1 & in_3;  // AND_Gate and_1, 32 bits wide
  Shifter #(.width(32)) shifter_1 (.in(in_3), .\dist (in_4), .out(shifter_1_out));
  assign xor_1_out = in_1 ^ in_3;  // XOR_Gate xor_1, 32 bits wide
  Multiplexer #(.select(4), .width(32)) multiplexer_1 (
    .in0(adder_1_out), .in1(and_1_out), .in4(shifter_1_out), .in9(xor_1_out), .out(in_2), .sel(in_5));  // open: in2, in3, in5, in6, in7, in8, in10, in11, in12, in13, in14, in15, en
endmodule

module \reg  (
  input  in_1,
  input  in_2,
  input  [31:0] in_3,
  input  [31:0] in_4,
  input  [4:0] in_5,
  input  [31:0] in_6,
  input  in_7,
  input  [4:0] in_8,
  input  [4:0] in_9,
  input  [31:0] in_10,
  input  [31:0] in_11,
  input  [31:0] in_12,
  input  [31:0] in_13
);

  wire decoder_1_out1, decoder_1_out2, decoder_1_out4, decoder_1_out8, decoder_1_out9, decoder_1_out31;
  wire [31:0] register_1_q, register_2_q, register_3_q, register_4_q, register_5_q, register_6_q, undriven;

  Decoder #(.select(5)) decoder_1 (
    .out1(decoder_1_out1), .out2(decoder_1_out2), .out4(decoder_1_out4), .out8(decoder_1_out8),
    .out9(decoder_1_out9), .out31(decoder_1_out31), .sel(in_9), .en(in_7));  // open: out0, out3, out5, out6, out7, out10, out11, out12, out13, out14, out15, out16, out17, out18, out19, out20, out21, out22, out23, out24, out25, out26, out27, out28, out29, out30
  Register #(.width(32)) register_1 (.D(in_3), .en(decoder_1_out1), .Q(register_1_q), .clk(in_1), .clr(in_2));
  Register #(.width(32)) register_2 (.D(in_3), .en(decoder_1_out2), .Q(register_2_q), .clk(in_1), .clr(in_2));
  Register #(.width(32)) register_3 (.D(in_3), .en(decoder_1_out4), .Q(register_3_q), .clk(in_1), .clr(in_2));
  Register #(.width(32)) register_4 (.D(in_3), .en(decoder_1_out8), .Q(register_4_q), .clk(in_1), .clr(in_2));
  Register #(.width(32)) register_5 (.D(in_3), .en(decoder_1_out9), .Q(register_5_q), .clk(in_1), .clr(in_2));
  Register #(.width(32)) register_6 (.D(in_3), .en(decoder_1_out31), .Q(register_6_q), .clk(in_1), .clr(in_2));
  Multiplexer #(.select(5), .width(32)) multiplexer_1 (
    .in0(undriven), .in1(register_1_q), .in2(register_2_q), .in6(register_3_q), .in10(register_4_q),
    .in11(register_5_q), .out(in_4), .sel(in_5));  // open: in3, in4, in5, in7, in8, in9, in12, in13, in14, in15, in16, in17, in18, in19, in20, in21, in22, in23, in24, in25, in26, in27, in28, in29, in30, in31, en
  Multiplexer #(.select(5), .width(32)) multiplexer_2 (
    .in0(undriven), .in1(register_1_q), .in2(register_2_q), .in4(register_3_q), .in8(register_4_q),
    .in9(register_5_q), .in31(register_6_q), .out(in_6), .sel(in_8));  // open: in3, in5, in6, in7, in10, in11, in12, in13, in14, in15, in16, in17, in18, in19, in20, in21, in22, in23, in24, in25, in26, in27, in28, in29, in30, en
  Multiplexer #(.select(5)) multiplexer_3 ();  // open: in0, in1, in2, in3, in4, in5, in6, in7, in8, in9, in10, in11, in12, in13, in14, in15, in16, in17, in18, in19, in20, in21, in22, in23, in24, in25, in26, in27, in28, in29, in30, in31, out, sel, en
endmodule
